// Logisim project PIN Locker.circ as structural Verilog: 11 circuits, main circuit Main
module deci_to_bcd (
  input  Y0,
  input  Y1,
  input  Y2,
  input  Y3,
  input  Y4,
  input  Y5,
  input  Y6,
  input  Y7,
  input  Y8,
  input  Y9,
  output a,
  output b,
  output c,
  output d
);

  or or_1 (a, Y9, Y8);
  or or_2 (b, Y5, Y4, Y6, Y7);
  or or_3 (c, Y6, Y3, Y2, Y7);
  or or_4 (d, Y9, Y7, Y1, Y5, Y3);

  // Notes on the sheet:
  //   Decimal to BCD encoder to storing
  //   a=  MSB
endmodule

module _4_bit_memory_block (
  input  [3:0] in_1,
  input  clear,
  output [3:0] out_3
);

  wire clock_1_out;

  Clock clock_1 (.out(clock_1_out));
  D_Flip_Flop d_ff_1 (.clk(clock_1_out), .D(in_1[3]), .Q(out_3[3]), .reset(clear));  // open: Qn, preset, en
  D_Flip_Flop d_ff_2 (.clk(clock_1_out), .D(in_1[2]), .Q(out_3[2]), .reset(clear));  // open: Qn, preset, en
  D_Flip_Flop d_ff_3 (.clk(clock_1_out), .D(in_1[1]), .Q(out_3[1]), .reset(clear));  // open: Qn, preset, en
  D_Flip_Flop d_ff_4 (.clk(clock_1_out), .D(in_1[0]), .Q(out_3[0]), .reset(clear));  // open: Qn, preset, en

  // Notes on the sheet:
  //   4 bit memory block (Modified right Shift register)
  //   A msb
endmodule

module _7_segment_display (
  input  A,
  input  B,
  input  C,
  input  D,
  output a_2,
  output b_2,
  output c_2,
  output d_2,
  output e,
  output f,
  output g
);

  wire and_1_out, and_2_out, and_3_out, and_4_out, and_5_out, and_6_out, and_7_out, and_8_out, and_9_out,
       and_10_out, and_11_out, and_12_out, and_13_out, and_14_out, and_15_out, and_16_out, and_17_out,
       and_18_out, and_19_out, and_20_out, and_21_out, and_22_out, and_23_out, and_24_out, and_25_out,
       not_1_out, not_2_out, not_3_out, not_4_out, not_5_out, not_6_out, not_7_out, not_8_out, not_9_out,
       not_10_out, not_11_out, not_12_out, not_13_out, not_14_out, not_15_out, not_16_out, not_17_out,
       not_18_out, not_19_out, not_20_out, not_21_out, not_22_out, not_23_out, not_24_out, not_25_out,
       not_26_out;

  not not_1 (not_1_out, A);
  not not_2 (not_2_out, B);
  and and_1 (and_1_out, not_1_out, not_2_out, D);
  not not_3 (not_3_out, A);
  and and_2 (and_2_out, not_3_out, B, not_4_out);
  not not_4 (not_4_out, D);
  and and_3 (and_3_out, B, C);
  and and_4 (and_4_out, A, not_5_out, not_6_out);
  not not_5 (not_5_out, B);
  not not_6 (not_6_out, C);
  and and_5 (and_5_out, A, not_7_out, not_8_out);
  not not_7 (not_7_out, B);
  not not_8 (not_8_out, D);
  not not_9 (not_9_out, C);
  and and_6 (and_6_out, not_9_out, D);
  not not_10 (not_10_out, A);
  and and_7 (and_7_out, not_10_out, not_11_out, C);
  not not_11 (not_11_out, B);
  not not_12 (not_12_out, A);
  and and_8 (and_8_out, not_12_out, B, not_13_out);
  not not_13 (not_13_out, C);
  not not_14 (not_14_out, B);
  and and_9 (and_9_out, A, not_14_out, not_15_out);
  not not_15 (not_15_out, D);
  not not_16 (not_16_out, C);
  and and_10 (and_10_out, not_16_out, D);
  and and_11 (and_11_out, C, not_17_out);
  not not_17 (not_17_out, D);
  not not_18 (not_18_out, A);
  and and_12 (and_12_out, not_18_out, not_19_out, D);
  not not_19 (not_19_out, B);
  not not_20 (not_20_out, B);
  and and_13 (and_13_out, not_20_out, not_21_out, D);
  not not_21 (not_21_out, C);
  and and_14 (and_14_out, B, not_22_out);
  not not_22 (not_22_out, D);
  and and_15 (and_15_out, B, C);
  and and_16 (and_16_out, A, C, not_23_out);
  not not_23 (not_23_out, D);
  not not_24 (not_24_out, B);
  and and_17 (and_17_out, not_24_out, D);
  and and_18 (and_18_out, C, D);
  and and_19 (and_19_out, A, B);
  not not_25 (not_25_out, C);
  and and_20 (and_20_out, not_25_out, D);
  and and_21 (and_21_out, B, C);
  and and_22 (and_22_out, A, C, not_26_out);
  not not_26 (not_26_out, D);
  and and_23 (and_23_out, C, D);
  and and_24 (and_24_out, A, D);
  and and_25 (and_25_out, A, C);
  or or_1 (a_2, and_1_out, and_2_out, and_3_out, and_4_out, and_5_out);
  or or_2 (b_2, and_6_out, and_7_out, and_8_out, and_9_out);
  or or_3 (c_2, and_10_out, and_11_out, B, A);
  or or_4 (d_2, and_12_out, and_13_out, and_14_out, and_15_out, and_16_out);
  or or_5 (e, and_17_out, and_18_out, and_19_out);
  or or_6 (f, and_20_out, and_21_out, and_22_out);
  or or_7 (g, and_23_out, B, and_24_out, and_25_out);

  // Notes on the sheet:
  //   for LED
  //   A =msb
endmodule

module Main (
);

  wire _0_out, _2_out, _3_out, _4_out, _5_out, _6_out, _7_out, _8_out, _9_out, and_1_out,
       bcd_to_excess_11_1_a_2, bcd_to_excess_11_1_b_2, bcd_to_excess_11_1_c_2, bcd_to_excess_11_1_d_2,
       button_out, clock_1_out, deci_to_excess_1_1_a, deci_to_excess_1_1_b, deci_to_excess_1_1_c,
       deci_to_excess_1_1_d, n7_segment_display_1_a_2, n7_segment_display_1_b_2, n7_segment_display_1_c_2,
       n7_segment_display_1_d_2, n7_segment_display_1_e, n7_segment_display_1_f, n7_segment_display_1_g,
       n7_segment_display_3_a_2, n7_segment_display_3_b_2, n7_segment_display_3_c_2,
       n7_segment_display_3_d_2, n7_segment_display_3_e, n7_segment_display_3_f, n7_segment_display_3_g,
       or_1_out, pattern_checker_1_out_4, pattern_checker_1_out_5, pattern_checker_1_out_6,
       pattern_checker_1_out_7, pattern_checker_1_out_8, R_out;
  wire [3:0] bit_extender_1_out, deci_to_bcd_1_d;

  _7_segment_display u_7_segment_display_1 (
    .A(deci_to_excess_1_1_a), .B(deci_to_excess_1_1_b), .C(deci_to_excess_1_1_c), .D(deci_to_excess_1_1_d),
    .a_2(n7_segment_display_1_a_2), .b_2(n7_segment_display_1_b_2), .c_2(n7_segment_display_1_c_2),
    .d_2(n7_segment_display_1_d_2), .e(n7_segment_display_1_e), .f(n7_segment_display_1_f),
    .g(n7_segment_display_1_g));
  deci_to_excess_1 deci_to_excess_1_1 (
    ._0(_0_out), ._1(button_out), ._2(_2_out), ._3(_3_out), ._4(_4_out), ._5(_5_out), ._6(_6_out),
    ._7(_7_out), ._8(_8_out), ._9(_9_out), .a(deci_to_excess_1_1_a), .b(deci_to_excess_1_1_b),
    .c(deci_to_excess_1_1_c), .d(deci_to_excess_1_1_d));
  _7_Segment_Display u_7_segment_display_2 (
    .g(n7_segment_display_1_g), .f(n7_segment_display_1_f), .a(n7_segment_display_1_a_2),
    .b(n7_segment_display_1_b_2), .e(n7_segment_display_1_e), .d(n7_segment_display_1_d_2),
    .c(n7_segment_display_1_c_2));  // open: dp
  Button button (.out(button_out));
  Button _4 (.out(_4_out));
  Button _7 (.out(_7_out));
  Button _3 (.out(_3_out));
  Button _2 (.out(_2_out));
  Button _6 (.out(_6_out));
  Button _5 (.out(_5_out));
  Button _9 (.out(_9_out));
  Button _8 (.out(_8_out));
  Button _0 (.out(_0_out));
  deci_to_bcd deci_to_bcd_1 (
    .a(deci_to_bcd_1_d[3]), .b(deci_to_bcd_1_d[2]), .c(deci_to_bcd_1_d[1]), .d(deci_to_bcd_1_d[0]),
    .Y0(_0_out), .Y1(button_out), .Y2(_2_out), .Y3(_3_out), .Y4(_4_out), .Y5(_5_out), .Y6(_6_out),
    .Y7(_7_out), .Y8(_8_out), .Y9(_9_out));
  Button R (.out(R_out));
  bcd_to_excess_11 bcd_to_excess_11_1 (
    .a(bit_extender_1_out[3]), .b(bit_extender_1_out[2]), .c(bit_extender_1_out[1]),
    .d(bit_extender_1_out[0]), .A_2(bcd_to_excess_11_1_a_2), .B_2(bcd_to_excess_11_1_b_2),
    .C_2(bcd_to_excess_11_1_c_2), .D_2(bcd_to_excess_11_1_d_2));
  or or_1 (or_1_out, deci_to_bcd_1_d[3], deci_to_bcd_1_d[2], deci_to_bcd_1_d[1], deci_to_bcd_1_d[0]);
  _7_segment_display u_7_segment_display_3 (
    .A(bcd_to_excess_11_1_a_2), .B(bcd_to_excess_11_1_b_2), .C(bcd_to_excess_11_1_c_2),
    .D(bcd_to_excess_11_1_d_2), .a_2(n7_segment_display_3_a_2), .b_2(n7_segment_display_3_b_2),
    .c_2(n7_segment_display_3_c_2), .d_2(n7_segment_display_3_d_2), .e(n7_segment_display_3_e),
    .f(n7_segment_display_3_f), .g(n7_segment_display_3_g));
  Clock clock_1 (.out(clock_1_out));
  Pattern_checker pattern_checker_1 (
    .in_1(deci_to_bcd_1_d), .out_6(pattern_checker_1_out_6), .out_8(pattern_checker_1_out_8),
    .out_5(pattern_checker_1_out_5), .out_7(pattern_checker_1_out_7), .out_4(pattern_checker_1_out_4),
    .reset(R_out), .Rep(or_1_out));
  _7_Segment_Display u_7_segment_display_4 (
    .g(n7_segment_display_3_g), .f(n7_segment_display_3_f), .a(n7_segment_display_3_a_2),
    .b(n7_segment_display_3_b_2), .e(n7_segment_display_3_e), .d(n7_segment_display_3_d_2),
    .c(n7_segment_display_3_c_2));  // open: dp
  and and_1 (and_1_out, pattern_checker_1_out_6, pattern_checker_1_out_8, pattern_checker_1_out_5, pattern_checker_1_out_7, pattern_checker_1_out_4);
  assign bit_extender_1_out = {{3{1'b0}}, and_1_out};  // Bit_Extender bit_extender_1

  // Notes on the sheet:
  //   33642
  //   Press Only 5 times
  //   n = Not matching
  //   o =Matched
  //   pattern checker
endmodule

module _4_bit_magnitude (
  input  A3,
  input  B3,
  input  Enabler,
  input  A2,
  input  B2,
  input  A1,
  input  B1,
  input  A0,
  input  B0,
  output a_b,
  output out_11,
  output A__B
);

  wire and_1_out, and_2_out, and_3_out, and_4_out, and_5_out, and_6_out, and_7_out, and_8_out, and_9_out,
       and_10_out, and_11_out, and_12_out, and_13_out, and_14_out, and_15_out, nor_1_out, nor_2_out,
       nor_3_out, nor_4_out, not_1_out, not_2_out, not_3_out, not_4_out, not_5_out, not_6_out, not_7_out,
       not_8_out, or_1_out, or_2_out;

  not not_1 (not_1_out, A2);
  not not_2 (not_2_out, B2);
  not not_3 (not_3_out, A1);
  not not_4 (not_4_out, B1);
  not not_5 (not_5_out, A0);
  not not_6 (not_6_out, B0);
  not not_7 (not_7_out, A3);
  not not_8 (not_8_out, B3);
  and and_1 (and_1_out, not_1_out, B2);
  and and_2 (and_2_out, A2, not_2_out);
  and and_3 (and_3_out, not_3_out, B1);
  and and_4 (and_4_out, A1, not_4_out);
  and and_5 (and_5_out, not_5_out, B0);
  and and_6 (and_6_out, A0, not_6_out);
  and and_7 (and_7_out, not_7_out, B3);
  and and_8 (and_8_out, A3, not_8_out);
  nor nor_1 (nor_1_out, and_5_out, and_6_out);
  nor nor_2 (nor_2_out, and_7_out, and_8_out);
  nor nor_3 (nor_3_out, and_1_out, and_2_out);
  nor nor_4 (nor_4_out, and_3_out, and_4_out);
  and and_9 (and_9_out, nor_2_out, and_1_out);
  and and_10 (and_10_out, nor_2_out, and_2_out);
  and and_11 (and_11_out, nor_2_out, nor_3_out, and_3_out);
  and and_12 (and_12_out, nor_2_out, nor_3_out, and_4_out);
  and and_13 (and_13_out, nor_2_out, nor_3_out, nor_4_out, and_5_out);
  and and_14 (and_14_out, nor_2_out, nor_3_out, nor_4_out, and_6_out);
  and and_15 (and_15_out, nor_2_out, nor_3_out, nor_4_out, nor_1_out);
  or or_1 (or_1_out, and_7_out, and_9_out, and_11_out, and_13_out);
  or or_2 (or_2_out, and_10_out, and_8_out, and_12_out, and_14_out);
  and and_16 (A__B, Enabler, and_15_out);
  and and_17 (a_b, Enabler, or_1_out);
  and and_18 (out_11, Enabler, or_2_out);

  // Notes on the sheet:
  //   a = user
  //   a0 = msb
  //   A>b
endmodule

module deci_to_excess_1 (
  input  _0,
  input  _1,
  input  _2,
  input  _3,
  input  _4,
  input  _5,
  input  _6,
  input  _7,
  input  _8,
  input  _9,
  output a,
  output b,
  output c,
  output d
);

  or u_A (d, _0, _2, _4, _6, _8);
  or u_B (c, _1, _2, _5, _6, _9);
  or u_C (b, _3, _4, _5, _6);
  or u_D (a, _7, _8, _9);

  // Notes on the sheet:
  //   a= msb
  //   to show input in LED
endmodule

// 1
module Pattern_checker (
  input  [3:0] in_1,
  input  Rep,
  input  reset,
  output out_4,
  output out_5,
  output out_6,
  output out_7,
  output out_8
);

  wire clock_1_out, clock_multiplier_1_out_3, enabler_1_out_3, enabler_1_out_4, enabler_1_out_5,
       enabler_1_out_6, enabler_1_out_7, n4_bit_magnitude_1_a__b, n4_bit_magnitude_2_a__b,
       n4_bit_magnitude_3_a__b, n4_bit_magnitude_4_a__b, n4_bit_magnitude_5_a__b;
  wire [3:0] n4_bit_memory_block_1_out_3, n4_bit_memory_block_2_out_3, n4_bit_memory_block_3_out_3,
       n4_bit_memory_block_4_out_3, n4_bit_memory_block_5_out_3;

  Enabler enabler_1 (
    .out_3(enabler_1_out_3), .out_4(enabler_1_out_4), .out_5(enabler_1_out_5), .out_6(enabler_1_out_6),
    .out_7(enabler_1_out_7), .clk(clock_multiplier_1_out_3), .clr(reset));
  Clock clock_1 (.out(clock_1_out));
  clock_multiplier clock_multiplier_1 (.in_1(Rep), .out_3(clock_multiplier_1_out_3));  // open: clear
  _4_bit_memory_block u_4_bit_memory_block_1 (.in_1(in_1), .out_3(n4_bit_memory_block_1_out_3));  // open: clear
  _4_bit_magnitude u_4_bit_magnitude_1 (
    .A3(n4_bit_memory_block_1_out_3[0]), .B3(1'b1), .A2(n4_bit_memory_block_1_out_3[1]), .B2(1'b1),
    .A1(n4_bit_memory_block_1_out_3[2]), .B1(1'b0), .A0(n4_bit_memory_block_1_out_3[3]), .B0(1'b0),
    .A__B(n4_bit_magnitude_1_a__b), .Enabler(enabler_1_out_3));  // open: a_b, out_11
  _4_bit_magnitude u_4_bit_magnitude_2 (
    .A3(n4_bit_memory_block_2_out_3[0]), .B3(1'b1), .A2(n4_bit_memory_block_2_out_3[1]), .B2(1'b1),
    .A1(n4_bit_memory_block_2_out_3[2]), .B1(1'b0), .A0(n4_bit_memory_block_2_out_3[3]), .B0(1'b0),
    .A__B(n4_bit_magnitude_2_a__b), .Enabler(enabler_1_out_4));  // open: a_b, out_11
  _4_bit_memory_block u_4_bit_memory_block_2 (
    .in_1(n4_bit_memory_block_1_out_3), .out_3(n4_bit_memory_block_2_out_3));  // open: clear
  Counter #(.width(1), .max('h1)) counter_1 (
    .load(1'b1), .D(1'b1), .count(1'b0), .Q(out_6), .clk(n4_bit_magnitude_1_a__b), .clr(reset));  // open: carry
  Counter #(.width(1), .max('h1)) counter_2 (
    .load(1'b1), .D(1'b1), .count(1'b0), .Q(out_8), .clk(n4_bit_magnitude_2_a__b), .clr(reset));  // open: carry
  _4_bit_memory_block u_4_bit_memory_block_3 (
    .in_1(n4_bit_memory_block_2_out_3), .out_3(n4_bit_memory_block_3_out_3));  // open: clear
  _4_bit_memory_block u_4_bit_memory_block_4 (
    .in_1(n4_bit_memory_block_3_out_3), .out_3(n4_bit_memory_block_4_out_3));  // open: clear
  _4_bit_magnitude u_4_bit_magnitude_3 (
    .A3(n4_bit_memory_block_3_out_3[0]), .B3(1'b0), .A2(n4_bit_memory_block_3_out_3[1]), .B2(1'b1),
    .A1(n4_bit_memory_block_3_out_3[2]), .B1(1'b1), .A0(n4_bit_memory_block_3_out_3[3]), .B0(1'b0),
    .A__B(n4_bit_magnitude_3_a__b), .Enabler(enabler_1_out_5));  // open: a_b, out_11
  _4_bit_magnitude u_4_bit_magnitude_4 (
    .A3(n4_bit_memory_block_4_out_3[0]), .B3(1'b0), .A2(n4_bit_memory_block_4_out_3[1]), .B2(1'b0),
    .A1(n4_bit_memory_block_4_out_3[2]), .B1(1'b1), .A0(n4_bit_memory_block_4_out_3[3]), .B0(1'b0),
    .A__B(n4_bit_magnitude_4_a__b), .Enabler(enabler_1_out_6));  // open: a_b, out_11
  _4_bit_memory_block u_4_bit_memory_block_5 (
    .in_1(n4_bit_memory_block_4_out_3), .out_3(n4_bit_memory_block_5_out_3));  // open: clear
  Counter #(.width(1), .max('h1)) counter_3 (
    .load(1'b1), .D(1'b1), .count(1'b0), .Q(out_5), .clk(n4_bit_magnitude_3_a__b), .clr(reset));  // open: carry
  Counter #(.width(1), .max('h1)) counter_4 (
    .load(1'b1), .D(1'b1), .count(1'b0), .Q(out_7), .clk(n4_bit_magnitude_4_a__b), .clr(reset));  // open: carry
  _4_bit_magnitude u_4_bit_magnitude_5 (
    .A3(n4_bit_memory_block_5_out_3[0]), .B3(1'b0), .A2(n4_bit_memory_block_5_out_3[1]), .B2(1'b1),
    .A1(n4_bit_memory_block_5_out_3[2]), .B1(1'b0), .A0(n4_bit_memory_block_5_out_3[3]), .B0(1'b0),
    .A__B(n4_bit_magnitude_5_a__b), .Enabler(enabler_1_out_7));  // open: a_b, out_11
  Counter #(.width(1), .max('h1)) counter_5 (
    .load(1'b1), .D(1'b1), .count(1'b0), .Q(out_4), .clk(n4_bit_magnitude_5_a__b), .clr(reset));  // open: carry

  // Notes on the sheet:
  //   enabler
  //   dec
  //   clk multiplier
  //   1st
  //   2nd
  //   3rd
  //   4th
  //   5th
endmodule

module Right_shift_register (
  input  in_1,
  input  clr,
  output out_3,
  output out_4,
  output out_5,
  output out_6,
  output out_7
);

  D_Flip_Flop d_ff_1 (.clk(in_1), .D(in_1), .Q(out_3), .reset(clr));  // open: Qn, preset, en
  D_Flip_Flop d_ff_2 (.clk(in_1), .D(out_3), .Q(out_4), .reset(clr));  // open: Qn, preset, en
  D_Flip_Flop d_ff_3 (.clk(in_1), .D(out_4), .Q(out_5), .reset(clr));  // open: Qn, preset, en
  D_Flip_Flop d_ff_4 (.clk(in_1), .D(out_5), .Q(out_6), .reset(clr));  // open: Qn, preset, en
  D_Flip_Flop d_ff_5 (.clk(in_1), .D(out_6), .Q(out_7), .reset(clr));  // open: Qn, preset, en
  D_Flip_Flop d_ff_6 (.clk(in_1), .D(out_7), .reset(clr));  // open: Q, Qn, preset, en

  // Notes on the sheet:
  //   in_1: pull=up
  //   will be used in Enabler and 4 bit memory block
endmodule

module clock_multiplier (
  input  in_1,
  input  clear,
  output out_3
);

  wire clock_1_out, d_ff_1_q, not_1_out;

  Clock clock_1 (.out(clock_1_out));
  D_Flip_Flop d_ff_1 (.clk(clock_1_out), .D(in_1), .Q(d_ff_1_q), .reset(clear));  // open: Qn, preset, en
  not not_1 (not_1_out, d_ff_1_q);
  and and_1 (out_3, in_1, not_1_out);

  // Notes on the sheet:
  //     pressing one clock  works 2 times
endmodule

module Enabler (
  input  clk,
  input  clr,
  output out_3,
  output out_4,
  output out_5,
  output out_6,
  output out_7
);

  wire d_ff_2_q, d_ff_4_q, d_ff_6_q, d_ff_7_q, d_ff_10_q, d_ff_11_q;

  not not_1 (out_3, d_ff_4_q);
  D_Flip_Flop d_ff_1 (.clk(clk), .D(clk), .Q(out_3), .reset(clr));  // open: Qn, preset, en
  D_Flip_Flop d_ff_2 (.clk(clk), .D(clk), .Q(d_ff_2_q), .reset(clr));  // open: Qn, preset, en
  not not_2 (out_4, d_ff_6_q);
  D_Flip_Flop d_ff_3 (.clk(clk), .D(out_3), .Q(out_4), .reset(clr));  // open: Qn, preset, en
  D_Flip_Flop d_ff_4 (.clk(clk), .D(d_ff_2_q), .Q(d_ff_4_q), .reset(clr));  // open: Qn, preset, en
  not not_3 (out_5, d_ff_7_q);
  D_Flip_Flop d_ff_5 (.clk(clk), .D(out_4), .Q(out_5), .reset(clr));  // open: Qn, preset, en
  D_Flip_Flop d_ff_6 (.clk(clk), .D(d_ff_4_q), .Q(d_ff_6_q), .reset(clr));  // open: Qn, preset, en
  D_Flip_Flop d_ff_7 (.clk(clk), .D(d_ff_6_q), .Q(d_ff_7_q), .reset(clr));  // open: Qn, preset, en
  not not_4 (out_6, d_ff_10_q);
  D_Flip_Flop d_ff_8 (.clk(clk), .D(out_5), .Q(out_6), .reset(clr));  // open: Qn, preset, en
  D_Flip_Flop d_ff_9 (.clk(clk), .D(out_6), .Q(out_7), .reset(clr));  // open: Qn, preset, en
  D_Flip_Flop d_ff_10 (.clk(clk), .D(d_ff_7_q), .Q(d_ff_10_q), .reset(clr));  // open: Qn, preset, en
  not not_5 (out_7, d_ff_11_q);
  D_Flip_Flop d_ff_11 (.clk(clk), .D(d_ff_10_q), .Q(d_ff_11_q), .reset(clr));  // open: Qn, preset, en
  D_Flip_Flop d_ff_12 (.clk(clk), .D(out_7), .reset(clr));  // open: Q, Qn, preset, en

  // Notes on the sheet:
  //   clk: pull=up
  //   for enabling
  //   (modified right shift register)
endmodule

module bcd_to_excess_11 (
  input  a,
  input  b,
  input  c,
  input  d,
  output A_2,
  output B_2,
  output C_2,
  output D_2
);

  wire not_1_out, not_2_out, not_3_out, not_4_out, not_5_out, not_6_out, not_7_out, not_8_out, not_9_out,
       not_10_out, not_11_out, not_12_out, not_13_out, not_14_out;

  not not_1 (not_1_out, a);
  not not_2 (not_2_out, b);
  not not_3 (not_3_out, c);
  not not_4 (not_4_out, a);
  not not_5 (not_5_out, b);
  not not_6 (not_6_out, c);
  not not_7 (not_7_out, a);
  not not_8 (not_8_out, b);
  not not_9 (not_9_out, c);
  not not_10 (not_10_out, d);
  not not_11 (not_11_out, a);
  not not_12 (not_12_out, b);
  not not_13 (not_13_out, c);
  not not_14 (not_14_out, d);
  and and_1 (A_2, not_1_out, not_2_out, not_3_out);
  and and_2 (B_2, not_4_out, not_5_out, not_6_out, d);
  and and_3 (C_2, not_7_out, not_8_out, not_9_out, not_10_out);
  and and_4 (D_2, not_11_out, not_12_out, not_13_out, not_14_out);

  // Notes on the sheet:
  //   A.a = msb
  //   to show output in LED
endmodule
